# Fritzing sketch garden-ai (saved by Fritzing 0.9.5d)

parts:
  WeMos_D1_Mini1 = WeMos D1 Mini
  Part1 = BH1750
  Part2 = FC-28 Soil Hygrometer Module
  Part3 = FC-28 Soil Hygrometer Module - Probe

nets:
  3V3: WeMos_D1_Mini1.3V3, Part1.VCC
  N1: WeMos_D1_Mini1.A0, Part2.AO
  N2: WeMos_D1_Mini1.D1, Part1.SCL
  N3: WeMos_D1_Mini1.D2, Part1.SDA
  N4: WeMos_D1_Mini1.G, Part1.GND
  N5: Part2.POS, Part3.POS
  N6: Part2.NEG, Part3.NEG

custom parts:
  BH1750: Light Sensor
  FC-28 Soil Hygrometer Module: The FC-28 is a soil hygrometer module that uses the Texas Instruments LM393 comparator chip to provide an analog measurement of soil humidity. The digital output is high when soil moisture is over a certain threshold, as determined by adjusting the potentiometer.
  FC-28 Soil Hygrometer Module - Probe: The FC-28 is a soil hygrometer module that uses the Texas Instruments LM393 comparator chip to provide an analog measurement of soil humidity.
